// Logisim project logisim.circ as structural Verilog: 1 circuit, main circuit LFSR
module LFSR (
  input  clk,
  output [3:0] out_2
);

  wire xor_1_out;

  D_Flip_Flop d_ff_1 (.D(xor_1_out), .clk(clk), .Q(out_2[0]));  // open: Qn, preset, reset
  D_Flip_Flop d_ff_2 (.D(out_2[0]), .clk(clk), .Q(out_2[1]));  // open: Qn, preset, reset
  xor xor_1 (xor_1_out, out_2[3], out_2[2]);
  D_Flip_Flop d_ff_3 (.D(out_2[1]), .clk(clk), .Q(out_2[2]));  // open: Qn, preset, reset
  D_Flip_Flop d_ff_4 (.D(out_2[2]), .clk(clk), .Q(out_2[3]));  // open: Qn, preset, reset
endmodule
